# Fritzing sketch Project IDEN (saved by Fritzing 0.9.5d)
breadboards: 1

parts:
  U1 = 74HC595 [package="DIP16 [THT]"]
  LED2 = LED - 5mm [color="Green (560nm)" package="5 mm [THT]"]
  Buzzer1 = Buzzer
  R4 = Resistor [tolerance=±5% resistance=1k package="2010 [SMD]"]
  PCB2 = RTC_DS1302_module
  Компонент3 = RFID-RC522-v3
  U2 = POT [package=alps_pot]
  LED1 = LED - 5mm [color="Red (633nm)" package="5 mm [THT]"]
  R5 = Resistor [tolerance=±5% resistance=220 package="2512 [SMD]"]
  R6 = Resistor [tolerance=±5% resistance=220 package="2512 [SMD]"]
  R7 = Resistor [tolerance=±5% resistance=220 package="2512 [SMD]"]
  LED3 = LED - 5mm [color="Yellow (595nm)" package="5 mm [THT]"]
  LCD1 = LCD screen
  Компонент1 = Arduino Uno (Rev3)
  microSD1 = MicroSD Card Module

nets:
  N1: U1.Q1, LCD1.RS
  N2: U1.Q3, LCD1.E
  N3: U1.Q4, LCD1.DB4
  N4: U1.Q5, LCD1.DB5
  N5: U1.Q6, LCD1.DB6
  N6: U1.Q7, LCD1.DB7
  GND: U1.GND, U1.OE, Buzzer1.pin2, PCB2.GND, Компонент3.GND, U2.E, R5.Pin_1, R6.Pin_1, R7.Pin_1, LCD1.VSS, LCD1.R/W, LCD1.LED+, Компонент1.GND, microSD1.GND
  VCC: U1.MR, U1.VCC, PCB2.VCC, U2.A, LCD1.VDD, LCD1.LED-, microSD1.VCC
  N7: U1.SH_CP, Компонент3.SCK, Компонент1.D13/SCK, microSD1.SCK
  N8: U1.ST_CP, Компонент1.D8
  N9: U1.DS, Компонент3.MOSI, Компонент1.D11_PWM/MOSI, microSD1.MOSI
  N10: LED2.cathode, R6.Pin_0
  N11: LED2.anode, Компонент1.A4/SDA
  N12: Buzzer1.pin1, R4.Pin_0
  N13: R4.Pin_1, Компонент1.A3
  N14: PCB2.RST, Компонент1.A0
  N15: PCB2.DAT, Компонент1.A1
  N16: PCB2.CLK, Компонент1.A2
  N17: Компонент3.SDA, Компонент1.D10_PWM/SS
  N18: Компонент3.MISO, Компонент1.D12/MISO, microSD1.MISO
  N19: Компонент3.RST, Компонент1.D9_PWM
  3.3V: Компонент3.3.3V, Компонент1.3V3
  N20: U2.S, LCD1.V0
  N21: LED1.cathode, R7.Pin_0
  N22: LED1.anode, Компонент1.A5/SCL
  N23: R5.Pin_0, LED3.cathode
  N24: LED3.anode, Компонент1.D6_PWM
  N25: Компонент1.D7, microSD1.CS

notes:
  13-SCK
  12-MISO
  11-MOSI
  Пока желтого нету (может и не будет)

custom parts:
  RTC_DS1302_module: Arduino module DS1302 SPI Real Time Clock
  RFID-RC522-v3: A simple China made RFID-RC522 Reader (6x4 cm); do check the pin labels, as this is a MFRC522 based clone.
